// Logisim project Cofre.circ as structural Verilog
module Registrador_de_Estado (
  input  CLK,
  input  N3,
  input  N2,
  input  N1,
  input  N0,
  output S3,
  output S2,
  output S1,
  output S0
);

  D_Flip_Flop d_ff_1 (.clk(CLK), .D(N3), .Q(S3));  // open: Qn, preset, en, reset
  D_Flip_Flop d_ff_2 (.clk(CLK), .D(N2), .Q(S2));  // open: Qn, preset, en, reset
  D_Flip_Flop d_ff_3 (.clk(CLK), .D(N1), .Q(S1));  // open: Qn, preset, en, reset
  D_Flip_Flop d_ff_4 (.clk(CLK), .D(N0), .Q(S0));  // open: Qn, preset, en, reset
endmodule
