// Logisim project Contador_Inteligente.circ as structural Verilog
module main (
  input  in_1,
  input  in_2,
  input  in_3,
  input  in_4,
  input  in_5,
  input  in_6,
  input  in_7,
  input  in_8,
  input  in_9,
  input  in_10,
  input  in_11,
  input  in_12,
  input  in_13,
  input  in_14,
  input  in_15,
  output [3:0] LSB,
  output [3:0] MSB,
  output [3:0] DEZENAS,
  output [3:0] CENTENAS,
  output [3:0] out_20,
  output [3:0] DEZENAS_2
);

  MX_MI mx_mi_1 (
    .UNIDADES(DEZENAS_2), .UNIDADES_2(LSB), .DEZENAS_3(CENTENAS), .DEZENAS_4(DEZENAS), .in_1(in_5),
    .out_14(MSB), .out_15(out_20), .DEZENAS({in_15, in_14, in_13, in_12}),
    .DEZENAS_2({in_15, in_14, in_13, in_12}), .in_6({in_11, in_9, in_7, in_6}),
    .in_7({in_11, in_9, in_7, in_6}), .in_2(in_10), .in_3(in_8), .in_8({in_4, in_3, in_2, in_1}),
    .in_9({in_4, in_3, in_2, in_1}));

  // Other names for the same wires on the sheet: A0C = in_12; A1C = in_13; A2C = in_14; A3C = in_15; A0D = in_6;
  //   A1D = in_7; A2D = in_9; A3D = in_11; A0U = in_1; A1U = in_2; A2U = in_3; A3U = in_4

  // Notes on the sheet:
  //   UNIDADES
  //   DEZENAS
  //   CENTENAS
  //   CENTENAS
  //   MSB
  //   UNIDADES
  //   LSB
  //   UNIDADES
endmodule

module Armazenador_de_bits_Com_LOAD (
  input  in_1,
  input  in_2,
  input  in_3,
  input  in_4,
  input  in_5,
  input  in_6,
  input  in_7,
  input  in_8,
  input  in_9,
  input  in_10,
  input  in_11,
  input  in_12,
  input  in_13,
  input  in_14,
  output LSB,
  output LSB_2,
  output LSB_3,
  output out_18,
  output out_19,
  output out_20,
  output out_21,
  output out_22,
  output out_23,
  output out_24,
  output MSB,
  output MSB_2
);

  wire multiplexer_1_out, multiplexer_2_out, multiplexer_3_out, multiplexer_4_out, multiplexer_5_out,
       multiplexer_6_out, multiplexer_7_out, multiplexer_8_out, multiplexer_9_out, multiplexer_10_out,
       multiplexer_11_out, multiplexer_12_out;

  D_Flip_Flop d_ff_1 (.clk(in_13), .D(multiplexer_1_out), .Q(LSB));  // open: Qn, preset, en, reset
  Multiplexer #(.enable("false")) multiplexer_1 (.in0(LSB), .in1(in_1), .out(multiplexer_1_out), .sel(in_14));
  D_Flip_Flop d_ff_2 (.clk(in_13), .D(multiplexer_2_out), .Q(out_18));  // open: Qn, preset, en, reset
  Multiplexer #(.enable("false")) multiplexer_2 (.in0(out_18), .in1(in_4), .out(multiplexer_2_out), .sel(in_14));
  D_Flip_Flop d_ff_3 (.clk(in_13), .D(multiplexer_3_out), .Q(out_21));  // open: Qn, preset, en, reset
  Multiplexer #(.enable("false")) multiplexer_3 (.in0(out_21), .in1(in_7), .out(multiplexer_3_out), .sel(in_14));
  D_Flip_Flop d_ff_4 (.clk(in_13), .D(multiplexer_4_out), .Q(out_24));  // open: Qn, preset, en, reset
  Multiplexer #(.enable("false")) multiplexer_4 (.in0(out_24), .in1(in_10), .out(multiplexer_4_out), .sel(in_14));
  D_Flip_Flop d_ff_5 (.clk(in_13), .D(multiplexer_5_out), .Q(LSB_2));  // open: Qn, preset, en, reset
  Multiplexer #(.enable("false")) multiplexer_5 (.in0(LSB_2), .in1(in_2), .out(multiplexer_5_out), .sel(in_14));
  D_Flip_Flop d_ff_6 (.clk(in_13), .D(multiplexer_6_out), .Q(out_19));  // open: Qn, preset, en, reset
  Multiplexer #(.enable("false")) multiplexer_6 (.in0(out_19), .in1(in_5), .out(multiplexer_6_out), .sel(in_14));
  D_Flip_Flop d_ff_7 (.clk(in_13), .D(multiplexer_7_out), .Q(out_22));  // open: Qn, preset, en, reset
  Multiplexer #(.enable("false")) multiplexer_7 (.in0(out_22), .in1(in_8), .out(multiplexer_7_out), .sel(in_14));
  D_Flip_Flop d_ff_8 (.clk(in_13), .D(multiplexer_8_out), .Q(MSB));  // open: Qn, preset, en, reset
  Multiplexer #(.enable("false")) multiplexer_8 (.in0(MSB), .in1(in_11), .out(multiplexer_8_out), .sel(in_14));
  Multiplexer #(.enable("false")) multiplexer_9 (.in0(out_23), .in1(in_9), .out(multiplexer_9_out), .sel(in_14));
  Multiplexer #(.enable("false")) multiplexer_10 (.in0(MSB_2), .in1(in_12), .out(multiplexer_10_out), .sel(in_14));
  D_Flip_Flop d_ff_9 (.clk(in_13), .D(multiplexer_11_out), .Q(LSB_3));  // open: Qn, preset, en, reset
  Multiplexer #(.enable("false")) multiplexer_11 (.in0(LSB_3), .in1(in_3), .out(multiplexer_11_out), .sel(in_14));
  D_Flip_Flop d_ff_10 (.clk(in_13), .D(multiplexer_12_out), .Q(out_20));  // open: Qn, preset, en, reset
  Multiplexer #(.enable("false")) multiplexer_12 (.in0(out_20), .in1(in_6), .out(multiplexer_12_out), .sel(in_14));
  D_Flip_Flop d_ff_11 (.clk(in_13), .D(multiplexer_9_out), .Q(out_23));  // open: Qn, preset, en, reset
  D_Flip_Flop d_ff_12 (.clk(in_13), .D(multiplexer_10_out), .Q(MSB_2));  // open: Qn, preset, en, reset

  // Other names for the same wires on the sheet: CLK = in_13; LOAD = in_14

  // Notes on the sheet:
  //   A0
  //   ENTRADA DE CLK
  //   MSB
  //   ENTRADA DE LOAD
  //   A1
  //   A2
endmodule

module MX_MI (
  input  in_1,
  input  in_2,
  input  in_3,
  input  [3:0] DEZENAS,
  input  [3:0] DEZENAS_2,
  input  [3:0] in_6,
  input  [3:0] in_7,
  input  [3:0] in_8,
  input  [3:0] in_9,
  output [3:0] UNIDADES,
  output [3:0] UNIDADES_2,
  output [3:0] DEZENAS_3,
  output [3:0] DEZENAS_4,
  output [3:0] out_14,
  output [3:0] out_15
);

  wire and_1_out, and_2_out, not_1_out;

  and and_1 (and_1_out, in_1, in_2);
  Armazenador_de_bits_Com_LOAD armazenador_de_bits_com_load_1 (
    .in_13(and_1_out), .in_14(in_3), .in_3(DEZENAS_2[0]), .LSB_3(out_15[0]), .out_20(out_15[1]),
    .in_6(DEZENAS_2[1]), .out_23(out_15[2]), .in_9(DEZENAS_2[2]), .MSB_2(out_15[3]), .in_12(DEZENAS_2[3]),
    .LSB(UNIDADES_2[0]), .in_1(in_9[0]), .out_18(UNIDADES_2[1]), .in_4(in_9[1]), .out_21(UNIDADES_2[2]),
    .out_24(UNIDADES_2[3]), .in_10(in_9[3]), .LSB_2(DEZENAS_4[0]), .in_2(in_7[0]), .out_19(DEZENAS_4[1]),
    .in_5(in_7[1]), .out_22(DEZENAS_4[2]), .in_8(in_7[2]), .MSB(DEZENAS_4[3]), .in_11(in_7[3]), .in_7(in_9[2]));
  and and_2 (and_2_out, in_1, not_1_out);
  not not_1 (not_1_out, in_2);
  Armazenador_de_bits_Com_LOAD armazenador_de_bits_com_load_2 (
    .in_13(and_2_out), .in_14(in_3), .in_3(DEZENAS[0]), .LSB_3(out_14[0]), .out_20(out_14[1]),
    .in_6(DEZENAS[1]), .out_23(out_14[2]), .in_9(DEZENAS[2]), .MSB_2(out_14[3]), .in_12(DEZENAS[3]),
    .LSB(UNIDADES[0]), .in_1(in_8[0]), .out_18(UNIDADES[1]), .in_4(in_8[1]), .out_21(UNIDADES[2]),
    .out_24(UNIDADES[3]), .in_10(in_8[3]), .LSB_2(DEZENAS_3[0]), .in_2(in_6[0]), .out_19(DEZENAS_3[1]),
    .in_5(in_6[1]), .out_22(DEZENAS_3[2]), .in_8(in_6[2]), .MSB(DEZENAS_3[3]), .in_11(in_6[3]), .in_7(in_8[2]));

  // Other names for the same wires on the sheet: CLK = in_1; LOAD = in_3; MX_MI = in_2

  // Notes on the sheet:
  //   CENTENAS
  //   CENTENAS
  //   MÁXIMO
  //   UNIDADES
  //   CENTENAS
  //   CENTENAS
  //   MÍNIMO
  //   UNIDADES
  //   ENTRADA DE CLK
  //   ENTRADA MX_MI
  //   ENTRADA DE LOAD
endmodule

module Contador (
  input  in_1,
  input  [3:0] in_2,
  input  [3:0] in_3,
  input  [3:0] in_4,
  input  [3:0] in_5,
  output [3:0] out_6,
  output [3:0] out_7,
  output [3:0] out_8
);

  wire A, a_t, AC, B, b_t, BC, C, c_t, CC, clock_1_out, clock_2_out, clock_3_out, D, d_t, DC, E, e_t, EC, F,
       f_t, FC, G, g_t, GC, pull_resistor_1_node, pull_resistor_2_node, somador_bcd_1_out_4,
       somador_bcd_2_out_4, somador_bcd_3_out_4;
  wire [3:0] armazenador_de_bits_1_a0, armazenador_de_bits_2_a0, armazenador_de_bits_3_a0, multiplexer_1_out,
       multiplexer_2_out, multiplexer_3_out;

  Multiplexer #(.width(4), .disabled(0), .enable("false")) multiplexer_1 (
    .in0(out_6), .in1(in_2), .out(multiplexer_1_out), .sel(in_1));
  Clock clock_1 (.out(clock_1_out));
  Armazenador_de_bits armazenador_de_bits_1 (
    .in_1(multiplexer_1_out[0]), .in_2(clock_1_out), .in_3(multiplexer_1_out[1]),
    .in_4(multiplexer_1_out[2]), .in_5(multiplexer_1_out[3]), .A0(armazenador_de_bits_1_a0[0]),
    .A1(armazenador_de_bits_1_a0[1]), .A2(armazenador_de_bits_1_a0[2]), .A3(armazenador_de_bits_1_a0[3]));
  Pull_Resistor pull_resistor_1 (.node(pull_resistor_1_node));
  Clock clock_2 (.out(clock_2_out));
  Armazenador_de_bits armazenador_de_bits_2 (
    .in_1(multiplexer_2_out[0]), .in_2(clock_2_out), .in_3(multiplexer_2_out[1]),
    .in_4(multiplexer_2_out[2]), .in_5(multiplexer_2_out[3]), .A0(armazenador_de_bits_2_a0[0]),
    .A1(armazenador_de_bits_2_a0[1]), .A2(armazenador_de_bits_2_a0[2]), .A3(armazenador_de_bits_2_a0[3]));
  Clock clock_3 (.out(clock_3_out));
  Armazenador_de_bits armazenador_de_bits_3 (
    .in_1(multiplexer_3_out[0]), .in_2(clock_3_out), .in_3(multiplexer_3_out[1]),
    .in_4(multiplexer_3_out[2]), .in_5(multiplexer_3_out[3]), .A0(armazenador_de_bits_3_a0[0]),
    .A1(armazenador_de_bits_3_a0[1]), .A2(armazenador_de_bits_3_a0[2]), .A3(armazenador_de_bits_3_a0[3]));
  Somador_bcd somador_bcd_1 (
    .in_2(armazenador_de_bits_1_a0), .in_3(in_3), .out_5(out_6), .out_4(somador_bcd_1_out_4),
    .in_1(pull_resistor_1_node));
  Multiplexer #(.width(4), .disabled(0), .enable("false")) multiplexer_2 (
    .in1(out_7), .out(multiplexer_2_out), .sel(somador_bcd_1_out_4));  // open: in0
  Multiplexer #(.width(4), .disabled(0), .enable("false")) multiplexer_3 (
    .in1(out_8), .out(multiplexer_3_out), .sel(somador_bcd_2_out_4));  // open: in0
  Somador_bcd somador_bcd_2 (
    .in_2(armazenador_de_bits_2_a0), .in_3(in_4), .out_5(out_7), .out_4(somador_bcd_2_out_4),
    .in_1(somador_bcd_1_out_4));
  Somador_bcd somador_bcd_3 (
    .in_2(armazenador_de_bits_3_a0), .in_3(in_5), .out_5(out_8), .out_4(somador_bcd_3_out_4),
    .in_1(somador_bcd_2_out_4));
  _7_Segment_Display u_7_segment_display_1 (.g(GC), .f(FC), .a(AC), .b(BC), .e(EC), .d(DC), .c(CC));  // open: dp
  Pull_Resistor #(.pull(1)) pull_resistor_2 (.node(pull_resistor_2_node));
  _7_Segment_Display u_7_segment_display_2 (.g(G), .f(F), .a(A), .b(B), .e(E), .d(D), .c(C));  // open: dp
  // _7448 7448_1: pin names not known; wires that end beside it: out_6[1], out_6[2], pull_resistor_2_node, pull_resistor_2_node, pull_resistor_2_node, out_6[3], out_6[0], f_t, g_t, a_t, b_t, c_t, d_t, e_t
  _7_Segment_Display u_7_segment_display_3 (.g(g_t), .f(f_t), .a(a_t), .b(b_t), .e(e_t), .d(d_t), .c(c_t));  // open: dp
  // _7448 7448_2: pin names not known; wires that end beside it: out_7[1], out_7[2], pull_resistor_2_node, pull_resistor_2_node, pull_resistor_2_node, out_7[3], out_7[0], F, G, A, B, C, D, E
  // _7448 7448_3: pin names not known; wires that end beside it: out_8[1], out_8[2], pull_resistor_2_node, pull_resistor_2_node, pull_resistor_2_node, out_8[3], out_8[0], FC, GC, AC, BC, CC, DC, EC
endmodule

module Armazenador_de_bits (
  input  in_1,
  input  in_2,
  input  in_3,
  input  in_4,
  input  in_5,
  output A0,
  output A1,
  output A2,
  output A3
);

  D_Flip_Flop d_ff_1 (.clk(in_2), .D(in_1), .Q(A0));  // open: Qn, preset, en, reset
  D_Flip_Flop d_ff_2 (.clk(in_2), .D(in_3), .Q(A1));  // open: Qn, preset, en, reset
  D_Flip_Flop d_ff_3 (.clk(in_2), .D(in_4), .Q(A2));  // open: Qn, preset, en, reset
  D_Flip_Flop d_ff_4 (.clk(in_2), .D(in_5), .Q(A3));  // open: Qn, preset, en, reset

  // Other names for the same wires on the sheet: CLK = in_2

  // Notes on the sheet:
  //   ENTRADA DE CLK
  //   LSB
  //   MSB
endmodule

module Somador_bcd (
  input  in_1,
  input  [3:0] in_2,
  input  [3:0] in_3,
  output out_4,
  output [3:0] out_5
);

  wire c, comparador_de_mag_1_out_11, or_2_out, S0, S1, S2, S3, somador_4bits_1_lsb_3, somador_4bits_1_msb_3,
       somador_4bits_1_out_11, somador_4bits_1_out_12, somador_completo_1_co, somador_completo_2_co,
       somador_completo_3_co, somador_completo_4_co;

  Somador_completo somador_completo_1 (.A(in_2[0]), .B(in_3[0]), .cin(in_1), .co(somador_completo_1_co), .s(S0));
  Somador_completo somador_completo_2 (
    .A(in_2[1]), .B(in_3[1]), .cin(somador_completo_1_co), .co(somador_completo_2_co), .s(S1));
  Somador_completo somador_completo_3 (
    .A(in_2[2]), .B(in_3[2]), .cin(somador_completo_2_co), .co(somador_completo_3_co), .s(S2));
  Somador_completo somador_completo_4 (
    .A(in_2[3]), .B(in_3[3]), .cin(somador_completo_3_co), .co(somador_completo_4_co), .s(S3));
  or or_1 (out_4, somador_completo_4_co, c);
  comparador_de_mag comparador_de_mag_1 (
    .A0(S0), .B0(1'b1), .A1(S1), .B1(1'b0), .A2(S2), .B2(1'b0), .A3(S3), .B3(1'b1),
    .out_11(comparador_de_mag_1_out_11));  // open: out_9, out_10
  or or_2 (or_2_out, comparador_de_mag_1_out_11, somador_completo_4_co);
  Multiplexer #(.enable("false")) multiplexer_1 (.in0(S0), .in1(somador_4bits_1_lsb_3), .out(out_5[0]), .sel(or_2_out));
  Multiplexer #(.enable("false")) multiplexer_2 (
    .in0(S1), .in1(somador_4bits_1_out_11), .out(out_5[1]), .sel(or_2_out));
  somador_4bits somador_4bits_1 (
    .out_11(somador_4bits_1_out_11), .out_12(somador_4bits_1_out_12), .MSB_3(somador_4bits_1_msb_3),
    .MSB(1'b0), .in_2(1'b1), .LSB(1'b1), .in_4(1'b0), .MSB_2(S3), .in_6(S2), .LSB_2(S1), .in_8(S0),
    .LSB_3(somador_4bits_1_lsb_3), .in_9(or_2_out), .out_14(c));
  Multiplexer #(.enable("false")) multiplexer_3 (
    .in0(S2), .in1(somador_4bits_1_out_12), .out(out_5[2]), .sel(or_2_out));
  Multiplexer #(.enable("false")) multiplexer_4 (.in0(S3), .in1(somador_4bits_1_msb_3), .out(out_5[3]), .sel(or_2_out));

  // Other names for the same wires on the sheet: A0 = in_2[0]; A1 = in_2[1]; A2 = in_2[2]; A3 = in_2[3]; B0 = in_3[0];
  //   B1 = in_3[1]; B2 = in_3[2]; B3 = in_3[3]

  // Notes on the sheet:
  //   CARRY UNI OUT
  //   LSB
  //   MSB
endmodule
